# Fritzing sketch stepper-motor (saved by Fritzing 0.9.6b)
breadboards: 1

parts:
  U1 = NodeMCU V1.0
  YwRobot_Power_Supply1 = YwRobot Breadboard Power Supply [part_number=545043]
  Driver1 = 28BYJ-48 Driver Module [part_number=ULN2003 package=THT]
  SM1 = 28BYJ-48 Stepper Motor [part_number=28BYJ-48]  # not connected

nets:
  N1: U1.D1, Driver1.IN1
  N2: U1.D2, Driver1.IN2
  N3: U1.D3, Driver1.IN3
  N4: U1.D4, Driver1.IN4
  N5: U1.GND, YwRobot_Power_Supply1.GND#11, YwRobot_Power_Supply1.GND#12
  N6: U1.Vin, YwRobot_Power_Supply1.VCC#5, YwRobot_Power_Supply1.VCC#6
  N7: YwRobot_Power_Supply1.VCC#9, YwRobot_Power_Supply1.VCC#10, Driver1.Vmotor
  N8: YwRobot_Power_Supply1.GND#13, YwRobot_Power_Supply1.GND#14, Driver1.GND

custom parts:
  NodeMCU V1.0: ESP8266 based NodeMCU
  YwRobot Breadboard Power Supply: The YwRobot Breadboard Power Supply (MB-V2) has two power rails; they can be 5V or 3V3. Power to the module can be provided through the female USB socket or through the A10 (female) 2.1mm power jack.
  28BYJ-48 Driver Module: High-power ULN2003 Stepper Motor Driver Board Test Module For Arduino AVR SMD
  28BYJ-48 Stepper Motor: Unipolar Stepper Motor 28BYJ-48 Top coil - pink & orange Bottom coil - blue & yellow Common rail - red Connector pins: blue - pink - yellow - orange - red
